# Fritzing sketch trt_v1 (saved by Fritzing 0.9.5d)
circuit board: 11.9263cm x 9.13784cm

parts:
  WeMos_D1_Mini1 = WeMos D1 Mini
  ZS-042_RTC1 = ZS-042 RTC Module
  M1 = pcf8574 io expansion board [package=THT]
  LCD2004-I2C1 = LCD2004-I2C
  Keypad4x1 = Keypad Membran 4x4
  Bauteil1 = RFID-RC522-v2

nets:
  3V3: WeMos_D1_Mini1.3V3, Bauteil1.3.3V
  5V: WeMos_D1_Mini1.5V, ZS-042_RTC1.VCC#7, M1.VCC
  N1: WeMos_D1_Mini1.D0, Bauteil1.RST
  N2: WeMos_D1_Mini1.D1, ZS-042_RTC1.SCL#9, M1.SCL
  N3: WeMos_D1_Mini1.D2, ZS-042_RTC1.SDA#8, M1.SDA
  N4: WeMos_D1_Mini1.D5, Bauteil1.SCK
  N5: WeMos_D1_Mini1.D6, Bauteil1.MISO
  N6: WeMos_D1_Mini1.D7, Bauteil1.MOSI
  N7: WeMos_D1_Mini1.D8, Bauteil1.SDA
  GND: WeMos_D1_Mini1.G, ZS-042_RTC1.GND#6, M1.GND, Bauteil1.GND
  N8: ZS-042_RTC1.GND#0, LCD2004-I2C1.GND
  N9: ZS-042_RTC1.VCC#1, LCD2004-I2C1.VCC
  N10: ZS-042_RTC1.SDA#2, LCD2004-I2C1.SDA
  N11: ZS-042_RTC1.SCL#3, LCD2004-I2C1.SCL
  N12: M1.O0, Keypad4x1.Pin8
  N13: M1.O1, Keypad4x1.Pin7
  N14: M1.O2, Keypad4x1.Pin6
  N15: M1.O3, Keypad4x1.Pin5
  N16: M1.O4, Keypad4x1.Pin4
  N17: M1.O5, Keypad4x1.Pin3
  N18: M1.O6, Keypad4x1.Pin2
  N19: M1.O7, Keypad4x1.Pin1

custom parts:
  pcf8574 io expansion board: pcf8574 io expansion board.
  LCD2004-I2C: A standard character display with 4x20 characters. Comes in many colors with LCM2004 IIC attached.
  Keypad Membran 4x4: Membrane Keypad 4x4 Matrix
  RFID-RC522-v2: A simple China made RFID-RC522 Reader; do check the pin labels, as this is a MFRC522 based clone.
